// Logisim project StopWatch-Stage3.circ as structural Verilog: 3 circuits, main circuit stage1
module stage1 (
  input  OnOff,
  output OutStream
);

  T_Flip_Flop t_ff_1 (.T(1'b1), .clk(OnOff), .Q(OutStream));  // open: Qn, reset, preset
endmodule

module stage2 (
  input  OnOffButton,
  input  ResetButton,
  output SO1,
  output SO2,
  output SO3,
  output SO4,
  output ResetMain,
  output ResetNext,
  output CLK
);

  wire and_1_out, and_3_out, and_4_out, or_1_out, t_ff_1_q, t_ff_2_q, t_ff_3_q, t_ff_4_q;

  Clock clock_1 (.out(CLK));
  T_Flip_Flop t_ff_1 (.T(OnOffButton), .clk(CLK), .Q(t_ff_1_q), .reset(or_1_out));  // open: Qn, preset
  D_Flip_Flop d_ff_1 (.D(t_ff_1_q), .clk(CLK), .Q(SO1));  // open: Qn, preset, reset
  T_Flip_Flop t_ff_2 (.T(t_ff_1_q), .clk(CLK), .Q(t_ff_2_q), .reset(or_1_out));  // open: Qn, preset
  D_Flip_Flop d_ff_2 (.D(t_ff_2_q), .clk(CLK), .Q(SO2));  // open: Qn, preset, reset
  and and_1 (and_1_out, t_ff_1_q, t_ff_2_q);
  T_Flip_Flop t_ff_3 (.T(and_1_out), .clk(CLK), .Q(t_ff_3_q), .reset(or_1_out));  // open: Qn, preset
  D_Flip_Flop d_ff_3 (.D(t_ff_3_q), .clk(CLK), .Q(SO3));  // open: Qn, preset, reset
  and and_2 (ResetNext, SO1, SO4);
  and and_3 (and_3_out, and_1_out, t_ff_3_q);
  T_Flip_Flop t_ff_4 (.T(and_3_out), .clk(CLK), .Q(t_ff_4_q), .reset(or_1_out));  // open: Qn, preset
  D_Flip_Flop d_ff_4 (.D(t_ff_4_q), .clk(CLK), .Q(SO4));  // open: Qn, preset, reset
  and and_4 (and_4_out, t_ff_2_q, t_ff_4_q);
  or or_1 (or_1_out, and_4_out, ResetButton);
  Hex_Digit_Display hex_digit_display_1 (.value({SO4, SO3, SO2, SO1}));  // open: dp

  assign ResetMain = ResetButton;
endmodule

module stage3 (
  input  OnOffButton,
  input  ResetButton,
  output ST1,
  output ST2,
  output ST3,
  output SO1,
  output SO2,
  output SO3,
  output SO4,
  output ResetNext,
  output CLK,
  output ResetMain
);

  wire and_1_out, and_2_out, stage2_1_resetnext, t_ff_1_q, t_ff_2_q, t_ff_3_q;

  T_Flip_Flop t_ff_1 (.T(1'b1), .clk(stage2_1_resetnext), .Q(t_ff_1_q), .reset(ResetNext));  // open: Qn, preset
  D_Flip_Flop d_ff_1 (.D(t_ff_1_q), .clk(CLK), .Q(ST1));  // open: Qn, preset, reset
  T_Flip_Flop t_ff_2 (.T(t_ff_1_q), .clk(stage2_1_resetnext), .Q(t_ff_2_q), .reset(ResetNext));  // open: Qn, preset
  D_Flip_Flop d_ff_2 (.D(t_ff_2_q), .clk(CLK), .Q(ST2));  // open: Qn, preset, reset
  and and_1 (and_1_out, t_ff_1_q, t_ff_2_q);
  T_Flip_Flop t_ff_3 (.T(and_1_out), .clk(stage2_1_resetnext), .Q(t_ff_3_q), .reset(ResetNext));  // open: Qn, preset
  D_Flip_Flop d_ff_3 (.D(t_ff_3_q), .clk(CLK), .Q(ST3));  // open: Qn, preset, reset
  and and_2 (and_2_out, t_ff_2_q, t_ff_3_q);
  stage2 stage2_1 (
    .OnOffButton(OnOffButton), .ResetButton(ResetButton), .SO1(SO1), .SO2(SO2), .SO3(SO3), .SO4(SO4),
    .ResetMain(ResetMain), .ResetNext(stage2_1_resetnext), .CLK(CLK));
  Hex_Digit_Display hex_digit_display_1 (.value({1'b0, ST3, ST2, ST1}));  // open: dp
  Hex_Digit_Display hex_digit_display_2 (.value({SO4, SO3, SO2, SO1}));  // open: dp
  or or_1 (ResetNext, and_2_out, ResetMain);
endmodule
